# Fritzing sketch Schematic (saved by Fritzing 0.9.10b)
breadboards: 1

parts:
  WeMos_D1_Mini_Relay_Shield_V1 = WeMos D1 Mini Relay Shield V2
  LED1 = smd LED [color="Red (633nm)" package="1206 [SMD]"]
  Part1 = Arduino Uno (Rev3) - ICSP
  R2 = Resistor [tolerance=±5% resistance=220 package="0805 [SMD]"]
  J1 = Piezo Speaker
  V2 = DC Power [voltage=5]  # not connected
  J2 = Basic Servo
  RHT1 = Humidity and Temperature Sensor RHT03
  R3 = PHOTOCELL [package=photocell]

nets:
  GND: WeMos_D1_Mini_Relay_Shield_V1.G, Part1.GND, R2.Pin_1, J2.gnd, RHT1.GND_1, RHT1.GND_2, R3.P$1
  N1: LED1.cathode, R2.Pin_0
  N2: LED1.anode, Part1.A0
  N3: Part1.A1, R3.P$2
  N4: Part1.D5_PWM, J1.pin2
  N5: Part1.D7, RHT1.Data-signal
  VCC: Part1.5V, J2.vcc, RHT1.Vcc

// code stored in the sketch: test.ino
// Inisialisasi pin sensor
const int suhuPin = A0;
const int cahayaPin = A1;
const int hujanPin = A2;

// Inisialisasi pin output
const int kipasPin = 2;
const int lampuPin = 3;
const int tutupJendelaPin = 4;

void setup() {
  // Set pin output
  pinMode(kipasPin, OUTPUT);
  pinMode(lampuPin, OUTPUT);
  pinMode(tutupJendelaPin, OUTPUT);
  
  // Mulai serial communication
  Serial.begin(9600);
}

void loop() {
  // Baca nilai sensor suhu
  float suhu = analogRead(suhuPin);
  suhu = (suhu * 5.0) / 1024.0; // Konversi nilai analog menjadi voltase
  suhu = suhu * 100.0; // Konversi voltase menjadi derajat Celcius
  
  // Baca nilai sensor cahaya
  int cahaya = analogRead(cahayaPin);
  
  // Baca nilai sensor hujan
  int hujan = analogRead(hujanPin);
  
  // Cek suhu
  if (suhu >= 30) {
    digitalWrite(kipasPin, HIGH); // Nyalakan kipas
  } else {
    digitalWrite(kipasPin, LOW); // Matikan kipas
  }
  
  // Cek cahaya
  if (cahaya < 200) {
    digitalWrite(lampuPin, HIGH); // Nyalakan lampu
  } else {
    digitalWrite(lampuPin, LOW); // Matikan lampu
  }
  
  // Cek hujan
  if (hujan < 500) {
    digitalWrite(tutupJendelaPin, HIGH); // Tutup jendela
  } else {
    digitalWrite(tutupJendelaPin, LOW); // Buka jendela
  }
  
  // Tampilkan nilai sensor pada Serial Monitor
  Serial.print("Suhu: ");
  Serial.print(suhu);
  Serial.print(" C, Cahaya: ");
  Serial.print(cahaya);
  Serial.print(", Hujan: ");
  Serial.print(hujan);
  Serial.println();
  
  delay(1000); // Tunggu 1 detik sebelum membaca sensor lagi
}
